# Fritzing sketch hex-reader (saved by Fritzing 0.9.10b)
breadboards: 1

parts:
  Part1 = Arduino Nano (Rev3.0)
  SSD1306_OLED = Grove OLED 128x96
  U1 = 74HC165 [part_number=SN74LS165 package="DIP16 [THT]"]
  U2 = 74HC165 [part_number=SN74LS165 package="DIP16 [THT]"]

nets:
  N1: Part1.D2, U1.Q2, U2.Q2
  N2: Part1.D3, U1.Q1, U2.Q1
  N3: Part1.A5, SSD1306_OLED.SCL
  N4: Part1.A4, SSD1306_OLED.SDA
  N5: U1.Q7', U2.MR
  GND: U1.Q0, U2.Q0

custom parts:
  74HC165: 8-bit parallel-load shift registers
